# Fritzing sketch schematic (saved by Fritzing 0.9.6b)
breadboards: 1

parts:
  DRV_1 = DRV 8825 Stepper Motor Carrier, High Current [part_number="DRV 8825"]
  Power_plug1 = Power plug
  M1 = Stepper Motor - Bipolar
  L298N1 = L298N DC motor driver
  M2 = DC Motor
  C1 = Capacitor Polarized [package=cpol-radial-100uf-25v]
  Part1 = Arduino Uno (Rev3)
  C2 = Ceramic Capacitor [capacitance=100nF voltage=35V package="0805 [SMD, multilayer]"]
  C3 = Ceramic Capacitor [capacitance=100nF voltage=35V package="100 mil [THT, multilayer]"]
  C4 = Ceramic Capacitor [capacitance=100nF voltage=35V package="0805 [SMD, multilayer]"]
  DRV_2 = DRV 8825 Stepper Motor Carrier, High Current [part_number="DRV 8825"]  # not connected
  DRV_3 = DRV 8825 Stepper Motor Carrier, High Current [part_number="DRV 8825"]  # not connected
  C5 = Capacitor Polarized [package=cpol-radial-100uf-25v]
  C6 = Capacitor Polarized [package=cpol-radial-100uf-25v]
  C7 = Ceramic Capacitor [capacitance=100nF voltage=35V package="0805 [SMD, multilayer]"]
  C8 = Ceramic Capacitor [capacitance=100nF voltage=35V package="0805 [SMD, multilayer]"]
  C9 = Ceramic Capacitor [capacitance=100nF voltage=35V package="0805 [SMD, multilayer]"]
  C10 = Ceramic Capacitor [capacitance=100nF voltage=35V package="0805 [SMD, multilayer]"]
  M3 = Stepper Motor - Bipolar  # not connected
  M4 = Stepper Motor - Bipolar  # not connected
  Mod1 = Raspberry Pi 4B
  Part2 = SerLCD_16x2 [part_number=LCD-14073]

nets:
  N1: DRV_1.RESET, DRV_1.SLEEP, Part1.5V, C3.0
  N2: DRV_1.STEP, Part1.D13/SCK, C4.1
  N3: DRV_1.DIRECTION, Part1.D12/MISO, C2.1
  VCC: DRV_1.VOLTAGE_ST/_MT, Power_plug1.VCC, L298N1.12V, C1.-, C5.-, C6.-
  GND: DRV_1.GROUND_ST/_MT, Power_plug1.GND, L298N1.GND, C1.+, C5.+, C6.+
  N4: DRV_1.OUT_2B, M1.A
  N5: DRV_1.OUT_2A, M1.C
  N6: DRV_1.OUT_1A, M1.B
  N7: DRV_1.OUT_1B, M1.D
  N8: DRV_1.GROUND_LOG, Part1.GND, C2.0, C3.1, C4.0, C7.0, C8.0, C9.0, C10.0
  N9: L298N1.OUT3, M2.pin_2
  N10: L298N1.OUT4, M2.pin_1
  N11: L298N1.ENB, Part1.D3_PWM
  N12: L298N1.IN3, Part1.D2
  N13: L298N1.IN4, Part1.D4
  N14: Part1.D8, C10.1
  N15: Part1.D9_PWM, C9.1
  N16: Part1.D10_PWM/SS, C8.1
  N17: Part1.D11_PWM/MOSI, C7.1
  3V3: Mod1.3V3, Part2.VIN
  N18: Mod1.GPIO2, Part2.SDA
  N19: Mod1.GPIO3, Part2.SCL
  GND_2: Mod1.GND, Part2.GND

notes:
  to Raspberry Pi
  USB to Arduinio
  Power over USB C

custom parts:
  L298N DC motor driver: 2x DC motor driver with 78M05 positive voltage regulator (7..35 V) L298N: max 46 V, 2 A Set 5 V Enable jumper to enable 5 V regultor (needed for the L298N) and +5 V output at screw terminal or supply external +5 V at screw terminal Set ENA and/or ENB to +5 V to enable motor permanently or supply ENA and/or ENB with PWM signal IN1 and IN2 set rotation directory for motor A (OUT1/OUT2) IN2 and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
  SerLCD_16x2: The SparkFun SerLCD is an AVR-based, serial enabled LCD that provides a simple and cost effective solution for adding a 16x2 RGB on Black Liquid Crystal Display into your project. We’ve seriously overhauled the PCB design on the back of the screen by including an ATmega328P that handles all of the screen control, meaning a backpack is no longer needed! This display can now communicate in three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
